# Fritzing sketch genius ver 2.0 full (saved by Fritzing 0.9.9b)
breadboards: 1

parts:
  S1 = Pushbutton [package="[THT]"]
  S2 = Pushbutton [package="[THT]"]
  S3 = Pushbutton [package="[THT]"]
  S4 = Pushbutton [package="[THT]"]
  J1 = Piezo Speaker
  R5 = Resistor [tolerance=±5% resistance=100 power=0.25 package=THT]
  LED2 = LED - 5mm [color="Red (633nm)" current=0.030 package="5 mm [THT]"]
  LED3 = LED - 5mm [color="Blue (430nm)" current=0.030 package="5 mm [THT]"]
  LED4 = LED - 5mm [color="Yellow (585nm)" current=0.030 package="5 mm [THT]"]
  R6 = Resistor [tolerance=±5% resistance=100 power=0.25 package=THT]
  R7 = Resistor [tolerance=±5% resistance=100 power=0.25 package=THT]
  R8 = Resistor [tolerance=±5% resistance=100 power=0.25 package=THT]
  LED1 = smd LED [color="Green (555nm)" package="0603 [SMD]"]
  LED1_2 = smd LED [color="Green (555nm)" package="0805 [SMD]"]
  Componente1 = Arduino Uno (Rev3)
  R9 = Resistor [tolerance=±5% power=0.25 resistance=220 package=THT]

nets:
  N1: S1.Pin_1, S1.Pin_2, Componente1.D11_PWM/MOSI
  N2: S1.Pin_3, S1.Pin_4, S2.Pin_3, S2.Pin_4, S3.Pin_3, S3.Pin_4, S4.Pin_3, S4.Pin_4, J1.pin1, R5.Pin_1, R6.Pin_1, R7.Pin_1, R8.Pin_1, Componente1.GND
  N3: S2.Pin_1, S2.Pin_2, Componente1.D10_PWM/SS
  N4: S3.Pin_1, S3.Pin_2, Componente1.D9_PWM
  N5: S4.Pin_1, S4.Pin_2, Componente1.D8
  N6: J1.pin2, R9.Pin_1
  N7: R5.Pin_0, LED1.cathode, LED1_2.cathode
  N8: LED2.cathode, R6.Pin_0
  N9: LED2.anode, Componente1.D3_PWM
  N10: LED3.cathode, R7.Pin_0
  N11: LED3.anode, Componente1.D4
  N12: LED4.cathode, R8.Pin_0
  N13: LED4.anode, Componente1.D5_PWM
  N14: LED1.anode, LED1_2.anode, Componente1.D2
  N15: Componente1.D6_PWM, R9.Pin_0
