# Fritzing sketch genius ver 2.1 half (saved by Fritzing 0.9.9b)
breadboards: 1

parts:
  Componente1 = Arduino Uno (Rev3)
  LED1 = LED - 5mm [color="Green (565nm)" current=0.030 package="5 mm [THT]"]
  S1 = Pushbutton [package="[THT]"]
  R1 = Resistor [tolerance=±5% power=0.25 resistance=100 package=THT]
  LED2 = LED - 5mm [color="Blue (470nm)" current=0.030 package="5 mm [THT]"]
  LED3 = LED - 5mm [color="Red (633nm)" current=0.030 package="5 mm [THT]"]
  S2 = Pushbutton [package="[THT]"]
  LED4 = LED - 5mm [color="Yellow (595nm)" current=0.030 package="5 mm [THT]"]
  S3 = Pushbutton [package="[THT]"]
  S4 = Pushbutton [package="[THT]"]
  R2 = Resistor [tolerance=±5% power=0.25 resistance=100 package=THT]
  R3 = Resistor [tolerance=±5% power=0.25 resistance=100 package=THT]
  R4 = Resistor [tolerance=±5% power=0.25 resistance=100 package=THT]
  J1 = Piezo Speaker
  R5 = Resistor [tolerance=±5% power=0.25 resistance=220 package=THT]

nets:
  N1: Componente1.D8, S1.Pin_1, S1.Pin_2
  N2: Componente1.D9_PWM, S2.Pin_1, S2.Pin_2
  N3: Componente1.D10_PWM/SS, S3.Pin_1, S3.Pin_2
  N4: Componente1.D11_PWM/MOSI, S4.Pin_1, S4.Pin_2
  N5: Componente1.GND, S1.Pin_3, S1.Pin_4, R1.Pin_1, S2.Pin_3, S2.Pin_4, S3.Pin_3, S3.Pin_4, S4.Pin_3, S4.Pin_4, R2.Pin_1, R3.Pin_1, R4.Pin_1, J1.pin1
  N6: Componente1.D2, LED1.anode
  N7: Componente1.D3_PWM, LED3.anode
  N8: Componente1.D4, LED2.anode
  N9: Componente1.D5_PWM, LED4.anode
  N10: Componente1.D6_PWM, R5.Pin_0
  N11: LED1.cathode, R1.Pin_0
  N12: LED2.cathode, R2.Pin_0
  N13: LED3.cathode, R3.Pin_0
  N14: LED4.cathode, R4.Pin_0
  N15: J1.pin2, R5.Pin_1
